// Logisim project Sagui_vet.circ as structural Verilog: 7 circuits, main circuit banco_registradores
module banco_registradores (
  input  [7:0] C,
  input  Clk,
  input  En,
  input  [1:0] wr,
  input  [1:0] mv,
  input  [1:0] rra,
  input  [1:0] rrb,
  output [7:0] r0,
  output [7:0] r1,
  output [7:0] A,
  output [7:0] r2,
  output [7:0] B,
  output [7:0] r3
);

  wire and_1_out, and_2_out, and_3_out, and_4_out, and_5_out, and_6_out, and_7_out, and_8_out, and_9_out,
       and_10_out, and_11_out, and_12_out, demultiplexer_1_out0, demultiplexer_1_out1, demultiplexer_1_out2,
       demultiplexer_1_out3, not_1_out, not_2_out, not_3_out, not_4_out, not_5_out, not_6_out, not_7_out,
       not_8_out, not_9_out, or_1_out, or_2_out, or_3_out, or_4_out, or_5_out, or_6_out;
  wire [3:0] high;

  Demultiplexer #(.select(2)) demultiplexer_1 (
    .out0(demultiplexer_1_out0), .out1(demultiplexer_1_out1), .out2(demultiplexer_1_out2),
    .out3(demultiplexer_1_out3), .in(En), .sel(wr));
  Multiplexer #(.width(4)) multiplexer_1 (.in0(C[7:4]), .in1(C[3:0]), .out(high), .sel(mv[1]));
  not not_1 (not_1_out, mv[1]);
  and and_1 (and_1_out, not_1_out, demultiplexer_1_out1);
  and and_2 (and_2_out, demultiplexer_1_out1, mv[0]);
  not not_2 (not_2_out, mv[1]);
  and and_3 (and_3_out, not_2_out, demultiplexer_1_out1);
  and and_4 (and_4_out, demultiplexer_1_out1, not_3_out);
  not not_3 (not_3_out, mv[0]);
  not not_4 (not_4_out, mv[1]);
  and and_5 (and_5_out, not_4_out, demultiplexer_1_out2);
  and and_6 (and_6_out, demultiplexer_1_out2, mv[0]);
  not not_5 (not_5_out, mv[1]);
  and and_7 (and_7_out, not_5_out, demultiplexer_1_out2);
  and and_8 (and_8_out, demultiplexer_1_out2, not_6_out);
  not not_6 (not_6_out, mv[0]);
  not not_7 (not_7_out, mv[1]);
  and and_9 (and_9_out, not_7_out, demultiplexer_1_out3);
  and and_10 (and_10_out, demultiplexer_1_out3, mv[0]);
  not not_8 (not_8_out, mv[1]);
  and and_11 (and_11_out, not_8_out, demultiplexer_1_out3);
  and and_12 (and_12_out, demultiplexer_1_out3, not_9_out);
  not not_9 (not_9_out, mv[0]);
  or or_1 (or_1_out, and_1_out, and_2_out);
  or or_2 (or_2_out, and_3_out, and_4_out);
  or or_3 (or_3_out, and_5_out, and_6_out);
  or or_4 (or_4_out, and_7_out, and_8_out);
  or or_5 (or_5_out, and_9_out, and_10_out);
  or or_6 (or_6_out, and_11_out, and_12_out);
  Register #(.trigger("falling"), .width(4)) register_1 (.D(4'b0000), .en(1'b0), .clk(Clk), .Q(r0[7:4]));  // open: clr
  Register #(.trigger("falling"), .width(4)) register_2 (.D(4'b0000), .en(1'b0), .clk(Clk), .Q(r0[3:0]));  // open: clr
  Register #(.trigger("falling"), .width(4)) register_3 (.D(high), .en(or_1_out), .clk(Clk), .Q(r1[7:4]));  // open: clr
  Register #(.trigger("falling"), .width(4)) register_4 (
    .D(C[3:0]), .en(or_2_out), .clk(Clk), .Q(r1[3:0]));  // open: clr
  Register #(.trigger("falling"), .width(4)) register_5 (.D(high), .en(or_3_out), .clk(Clk), .Q(r2[7:4]));  // open: clr
  Register #(.trigger("falling"), .width(4)) register_6 (
    .D(C[3:0]), .en(or_4_out), .clk(Clk), .Q(r2[3:0]));  // open: clr
  Register #(.trigger("falling"), .width(4)) register_7 (.D(high), .en(or_5_out), .clk(Clk), .Q(r3[7:4]));  // open: clr
  Register #(.trigger("falling"), .width(4)) register_8 (
    .D(C[3:0]), .en(or_6_out), .clk(Clk), .Q(r3[3:0]));  // open: clr
  Multiplexer #(.select(2), .width(8)) multiplexer_2 (.in0(r0), .in1(r1), .in2(r2), .in3(r3), .out(A), .sel(rra));
  Multiplexer #(.select(2), .width(8)) multiplexer_3 (.in0(r0), .in1(r1), .in2(r2), .in3(r3), .out(B), .sel(rrb));
  // also tied to GND on the sheet: demultiplexer_1_out0

  // Other names for the same wires on the sheet: low[3:0] = C[3:0]; mvSel = mv[0]; mv_t = mv[1]
endmodule

module ALU_8bits (
  input  [2:0] func,
  input  [7:0] A,
  input  [7:0] B,
  output Zero,
  output [7:0] S
);

  wire or_1_out;
  wire [7:0] adder_1_out, and_1_out, shifter_8bits_1_s, subtractor_1_out;

  Adder adder_1 (.a(A), .b(B), .out(adder_1_out));  // open: cin, cout
  Subtractor subtractor_1 (.a(A), .b(B), .out(subtractor_1_out));  // open: bin, bout
  assign and_1_out = A & B;  // AND_Gate and_1, 8 bits wide
  Multiplexer #(.select(3), .width(8)) multiplexer_1 (
    .in0(adder_1_out), .in1(subtractor_1_out), .in2(and_1_out), .in3(shifter_8bits_1_s), .out(S), .sel(func));  // open: in4, in5, in6, in7
  shifter_8bits shifter_8bits_1 (.A(A), .B(B), .S(shifter_8bits_1_s));
  or or_1 (or_1_out, S[0], S[1], S[2], S[3], S[4], S[5], S[6], S[7]);
  not not_1 (Zero, or_1_out);
endmodule

module banco_registradores_vet (
  input  [7:0] C,
  input  [7:0] id,
  input  Clk,
  input  En,
  input  [1:0] wr,
  input  [1:0] mv,
  input  [1:0] rra,
  input  [1:0] rrb,
  output [7:0] r0,
  output [7:0] r1,
  output [7:0] A,
  output [7:0] r2,
  output [7:0] B,
  output [7:0] r3
);

  wire and_1_out, and_2_out, and_3_out, and_4_out, and_5_out, and_6_out, and_7_out, and_8_out, and_9_out,
       and_10_out, and_11_out, and_12_out, demultiplexer_1_out0, demultiplexer_1_out1, demultiplexer_1_out2,
       demultiplexer_1_out3, not_1_out, not_2_out, not_3_out, not_4_out, not_5_out, not_6_out, not_7_out,
       not_8_out, not_9_out, or_1_out, or_2_out, or_3_out, or_4_out, or_5_out, or_6_out;
  wire [3:0] high;

  Demultiplexer #(.select(2)) demultiplexer_1 (
    .out0(demultiplexer_1_out0), .out1(demultiplexer_1_out1), .out2(demultiplexer_1_out2),
    .out3(demultiplexer_1_out3), .in(En), .sel(wr));
  Multiplexer #(.width(4)) multiplexer_1 (.in0(C[7:4]), .in1(C[3:0]), .out(high), .sel(mv[1]));
  not not_1 (not_1_out, mv[1]);
  and and_1 (and_1_out, not_1_out, demultiplexer_1_out1);
  and and_2 (and_2_out, demultiplexer_1_out1, mv[0]);
  not not_2 (not_2_out, mv[1]);
  and and_3 (and_3_out, not_2_out, demultiplexer_1_out1);
  and and_4 (and_4_out, demultiplexer_1_out1, not_3_out);
  not not_3 (not_3_out, mv[0]);
  not not_4 (not_4_out, mv[1]);
  and and_5 (and_5_out, not_4_out, demultiplexer_1_out2);
  and and_6 (and_6_out, demultiplexer_1_out2, mv[0]);
  not not_5 (not_5_out, mv[1]);
  and and_7 (and_7_out, not_5_out, demultiplexer_1_out2);
  and and_8 (and_8_out, demultiplexer_1_out2, not_6_out);
  not not_6 (not_6_out, mv[0]);
  not not_7 (not_7_out, mv[1]);
  and and_9 (and_9_out, not_7_out, demultiplexer_1_out3);
  and and_10 (and_10_out, demultiplexer_1_out3, mv[0]);
  not not_8 (not_8_out, mv[1]);
  and and_11 (and_11_out, not_8_out, demultiplexer_1_out3);
  and and_12 (and_12_out, demultiplexer_1_out3, not_9_out);
  not not_9 (not_9_out, mv[0]);
  or or_1 (or_1_out, and_1_out, and_2_out);
  or or_2 (or_2_out, and_3_out, and_4_out);
  or or_3 (or_3_out, and_5_out, and_6_out);
  or or_4 (or_4_out, and_7_out, and_8_out);
  or or_5 (or_5_out, and_9_out, and_10_out);
  or or_6 (or_6_out, and_11_out, and_12_out);
  Register #(.trigger("high"), .width(4)) register_1 (.D(id[7:4]), .en(1'b1), .clk(Clk), .Q(r0[7:4]));  // open: clr
  Register #(.trigger("high"), .width(4)) register_2 (.D(id[3:0]), .en(1'b1), .clk(Clk), .Q(r0[3:0]));  // open: clr
  Register #(.trigger("falling"), .width(4)) register_3 (.D(high), .en(or_1_out), .clk(Clk), .Q(r1[7:4]));  // open: clr
  Register #(.trigger("falling"), .width(4)) register_4 (
    .D(C[3:0]), .en(or_2_out), .clk(Clk), .Q(r1[3:0]));  // open: clr
  Register #(.trigger("falling"), .width(4)) register_5 (.D(high), .en(or_3_out), .clk(Clk), .Q(r2[7:4]));  // open: clr
  Register #(.trigger("falling"), .width(4)) register_6 (
    .D(C[3:0]), .en(or_4_out), .clk(Clk), .Q(r2[3:0]));  // open: clr
  Register #(.trigger("falling"), .width(4)) register_7 (.D(high), .en(or_5_out), .clk(Clk), .Q(r3[7:4]));  // open: clr
  Register #(.trigger("falling"), .width(4)) register_8 (
    .D(C[3:0]), .en(or_6_out), .clk(Clk), .Q(r3[3:0]));  // open: clr
  Multiplexer #(.select(2), .width(8)) multiplexer_2 (.in0(r0), .in1(r1), .in2(r2), .in3(r3), .out(A), .sel(rra));
  Multiplexer #(.select(2), .width(8)) multiplexer_3 (.in0(r0), .in1(r1), .in2(r2), .in3(r3), .out(B), .sel(rrb));
  // also tied to GND on the sheet: demultiplexer_1_out0

  // Other names for the same wires on the sheet: low[3:0] = C[3:0]; mvSel = mv[0]; mv_t = mv[1]
endmodule

module main (
  output [7:0] out_1,
  output [7:0] out_2,
  output [7:0] out_3,
  output [7:0] out_4,
  output [7:0] out_5,
  output [7:0] out_6,
  output [7:0] out_7,
  output [7:0] out_8,
  output [7:0] out_9,
  output [7:0] out_10,
  output [7:0] out_11,
  output [7:0] out_12,
  output [7:0] out_13,
  output [7:0] out_14,
  output [7:0] out_15,
  output [7:0] out_16
);

  wire branch, branch_sc, button_1_out, clk, clock_1_out, multiplexer_1_out, multiplexer_6_out, mv, mv_sc,
       not_2_out, not_3_out, ramW, ramW_sc, sca_to_vet, sel, shift, src, src_sc, writeEn, writeEn_sc, zero;
  wire [0:0] mvSel, mvSel_sc;
  wire [2:0] Intruction_Memory_data;
  wire [3:0] func, func_sc, Imm;
  wire [7:0] adder_1_out, B, multiplexer_2_out, multiplexer_3_out, PC_q, processing_element_sca_1_r0,
       processing_element_sca_1_r1, processing_element_sca_1_r2, processing_element_sca_1_r3, sca_reg;
  wire [9:0] Control_Mem_data, multiplexer_4_out, multiplexer_5_out;

  ROM rom_1 ();  // open: addr, data
  Adder adder_1 (.a(PC_q), .b(8'h1), .out(adder_1_out));  // open: cin, cout
  Multiplexer multiplexer_1 (.in0(1'b0), .in1(branch_sc), .out(multiplexer_1_out), .sel(zero));
  Multiplexer #(.width(8)) multiplexer_2 (.in0(adder_1_out), .in1(B), .out(multiplexer_2_out), .sel(multiplexer_1_out));
  Clock clock_1 (.out(clock_1_out));
  not not_1 (clk, clock_1_out);
  Register PC (.D(multiplexer_2_out), .en(1'b1), .clk(clk), .Q(PC_q), .clr(button_1_out));
  Button button_1 (.out(button_1_out));
  ROM Intruction_Memory (.addr(PC_q), .data({sel, Intruction_Memory_data, Imm}));
  ROM #(.addrWidth(4), .dataWidth(10)) Control_Mem (.addr({sel, Intruction_Memory_data}), .data(Control_Mem_data));
  Multiplexer #(.width(8)) multiplexer_3 (
    .in0({4'b0000, Imm}), .in1(sca_reg), .out(multiplexer_3_out), .sel(sca_to_vet));
  and and_1 (sca_to_vet, Intruction_Memory_data[0], Intruction_Memory_data[1], Intruction_Memory_data[2], sel);
  and and_2 (shift, sel, Intruction_Memory_data[2], Intruction_Memory_data[1], not_2_out);
  not not_2 (not_2_out, Intruction_Memory_data[0]);
  Multiplexer #(.width(10)) multiplexer_4 (
    .in0(Control_Mem_data), .in1({10{1'b0}}), .out(multiplexer_4_out), .sel(sel));
  Multiplexer #(.width(10)) multiplexer_5 (
    .in0({10{1'b0}}), .in1(Control_Mem_data), .out(multiplexer_5_out), .sel(sel));
  Multiplexer multiplexer_6 (.in0(mv), .in1(not_3_out), .out(multiplexer_6_out), .sel(sca_to_vet));
  not not_3 (not_3_out, mv);
  Multiplexer #(.width(10)) multiplexer_7 (
    .in0(multiplexer_4_out), .in1(Control_Mem_data),
    .out({branch_sc, mv_sc, mvSel_sc[0], writeEn_sc, ramW_sc, src_sc, func_sc}), .sel(shift));
  Multiplexer #(.width(10)) multiplexer_8 (
    .in0(multiplexer_5_out), .in1({10{1'b0}}), .out({branch, mv, mvSel[0], writeEn, ramW, src, func}),
    .sel(shift));
  processing_element_vet processing_element_vet_1 (
    .ramW(ramW), .src(src), .ra(Imm[3:2]), .mvSel({sca_to_vet, mv, mvSel[0]}), .mv(multiplexer_6_out),
    .clk(clk), .imm(multiplexer_3_out), .writeEn(writeEn), .rb(Imm[1:0]), .id({8{1'b0}}), .func(func),
    .r0(out_1), .r1(out_2), .r2(out_3), .r3(out_4));
  processing_element_vet processing_element_vet_2 (
    .ramW(ramW), .src(src), .ra(Imm[3:2]), .mvSel({sca_to_vet, mv, mvSel[0]}), .mv(multiplexer_6_out),
    .clk(clk), .imm(multiplexer_3_out), .writeEn(writeEn), .rb(Imm[1:0]), .id(8'h1), .func(func), .r0(out_5),
    .r1(out_6), .r2(out_7), .r3(out_8));
  processing_element_vet processing_element_vet_3 (
    .ramW(ramW), .src(src), .ra(Imm[3:2]), .mvSel({sca_to_vet, mv, mvSel[0]}), .mv(multiplexer_6_out),
    .clk(clk), .imm(multiplexer_3_out), .writeEn(writeEn), .rb(Imm[1:0]), .id(8'h2), .func(func), .r0(out_9),
    .r1(out_10), .r2(out_11), .r3(out_12));
  processing_element_vet processing_element_vet_4 (
    .ramW(ramW), .src(src), .ra(Imm[3:2]), .mvSel({sca_to_vet, mv, mvSel[0]}), .mv(multiplexer_6_out),
    .clk(clk), .imm(multiplexer_3_out), .writeEn(writeEn), .rb(Imm[1:0]), .id(8'h3), .func(func),
    .r0(out_13), .r1(out_14), .r2(out_15), .r3(out_16));
  processing_element_sca processing_element_sca_1 (
    .mv(mv_sc), .imm({4'b0000, Imm}), .clk(clk), .writeEn(writeEn_sc), .mvSel({mv_sc, mvSel_sc[0]}),
    .ra(Imm[3:2]), .rb(Imm[1:0]), .ramW(ramW_sc), .src(src_sc), .func(func_sc), .branch(zero),
    .r0(processing_element_sca_1_r0), .r1(processing_element_sca_1_r1), .r2(processing_element_sca_1_r2),
    .r3(processing_element_sca_1_r3), .B(B));
  Multiplexer #(.select(2), .width(8)) multiplexer_9 (
    .in0(processing_element_sca_1_r0), .in1(processing_element_sca_1_r1), .in2(processing_element_sca_1_r2),
    .in3(processing_element_sca_1_r3), .out(sca_reg), .sel(Imm[1:0]));

  // Other names for the same wires on the sheet: mvSel[1] = mv; mvSel_sc[1] = mv_sc; ra[1:0] = Imm[3:2];
  //   rb[1:0] = Imm[1:0]

  // Notes on the sheet:
  //   contents of rom_1 (hex, n*v repeats v):
  //   34 49 e6
  //   contents of Intruction_Memory (hex, n*v repeats v):
  //   c8 34 49 33 5d 21 34 7d 20 33 4d 9b 20 31 4d ff f6 c9 33 71 a0 b8 c9 20 33 4d 20 36 5d 23 30 7d 20
  //   36 4d 9b 20 31 4d f7 a0 df cd f6 c9 21 3a 71 a0 b0 89 b3 8d cb b6 99 a0 b1 89 b4 8d cb b7 99 a0 b2
  //   89 b5 8d cb b8 99 24 39 71
  //   contents of Control_Mem (hex, n*v repeats v):
  //   50 20 1c0 140 40 41 42 200 50 20 1c0 140 40 41 43 40
endmodule

module processing_element_vet (
  input  [2:0] mvSel,
  input  [7:0] imm,
  input  [7:0] id,
  input  mv,
  input  ramW,
  input  clk,
  input  writeEn,
  input  [1:0] ra,
  input  src,
  input  [1:0] rb,
  input  [3:0] func,
  output [7:0] r0,
  output [7:0] r1,
  output [7:0] r2,
  output [7:0] r3
);

  wire [1:0] multiplexer_1_out, multiplexer_2_out;
  wire [7:0] banco_registradores_vet_1_a, banco_registradores_vet_1_b, C, multiplexer_3_out,
       multiplexer_4_out, ram_1_dout, S;

  Multiplexer #(.width(2)) multiplexer_1 (.in0(ra), .in1(2'b01), .out(multiplexer_1_out), .sel(mv));
  Multiplexer #(.width(2)) multiplexer_2 (.in0(multiplexer_1_out), .in1(ra), .out(multiplexer_2_out), .sel(mvSel[2]));
  Multiplexer #(.width(8)) multiplexer_3 (.in0(C), .in1(imm), .out(multiplexer_3_out), .sel(mv));
  banco_registradores_vet banco_registradores_vet_1 (
    .rrb(rb), .rra(ra), .Clk(clk), .En(writeEn), .mv(mvSel[1:0]), .C(multiplexer_3_out),
    .wr(multiplexer_2_out), .id(id), .B(banco_registradores_vet_1_b), .A(banco_registradores_vet_1_a),
    .r2(r2), .r0(r0), .r1(r1), .r3(r3));
  Multiplexer #(.width(8)) multiplexer_4 (
    .in0(banco_registradores_vet_1_b), .in1(imm), .out(multiplexer_4_out), .sel(func[3]));
  ALU_8bits alu_8bits_1 (
    .func(func[2:0]), .A(banco_registradores_vet_1_a), .B(multiplexer_4_out), .S(S));  // open: Zero
  RAM #(.asyncread("true"), .trigger("falling")) ram_1 (
    .addr(banco_registradores_vet_1_b), .we(ramW), .oe(1'b1), .clk(clk), .din(banco_registradores_vet_1_a),
    .dout(ram_1_dout));
  Multiplexer #(.width(8)) multiplexer_5 (.in0(S), .in1(ram_1_dout), .out(C), .sel(src));

  // Other names for the same wires on the sheet: func_t[2:0] = func[2:0]; stov = mvSel[2]; mvSel_t[1:0] = mvSel[1:0]
endmodule

module processing_element_sca (
  input  mv,
  input  [7:0] imm,
  input  clk,
  input  writeEn,
  input  [1:0] mvSel,
  input  [1:0] ra,
  input  [1:0] rb,
  input  ramW,
  input  src,
  input  [3:0] func,
  output branch,
  output [7:0] r0,
  output [7:0] r1,
  output [7:0] r2,
  output [7:0] r3,
  output [7:0] B
);

  wire not_1_out;
  wire [1:0] multiplexer_2_out;
  wire [7:0] alu_8bits_1_s, banco_registradores_1_a, C, multiplexer_1_out, nor_1_out, Seq_Data_Mem_dout;

  not not_1 (not_1_out, mv);
  Multiplexer #(.width(8)) multiplexer_1 (.in0(imm), .in1(C), .out(multiplexer_1_out), .sel(not_1_out));
  Multiplexer #(.width(2)) multiplexer_2 (.in0(ra), .in1(2'b01), .out(multiplexer_2_out), .sel(mv));
  banco_registradores banco_registradores_1 (
    .rrb(rb), .rra(ra), .Clk(clk), .En(writeEn), .mv(mvSel), .C(multiplexer_1_out), .wr(multiplexer_2_out),
    .B(B), .A(banco_registradores_1_a), .r2(r2), .r0(r0), .r1(r1), .r3(r3));
  assign nor_1_out = ~({8{1'b0}} | banco_registradores_1_a);  // NOR_Gate nor_1, 8 bits wide
  and and_1 (branch, nor_1_out[0], nor_1_out[1], nor_1_out[2], nor_1_out[3], nor_1_out[4], nor_1_out[5], nor_1_out[6], nor_1_out[7]);
  RAM Seq_Data_Mem (.addr(banco_registradores_1_a), .we(ramW), .oe(1'b1), .clk(clk), .din(B), .dout(Seq_Data_Mem_dout));
  ALU_8bits alu_8bits_1 (.func(func[2:0]), .A(banco_registradores_1_a), .B(B), .S(alu_8bits_1_s));  // open: Zero
  Multiplexer #(.width(8)) multiplexer_3 (.in0(alu_8bits_1_s), .in1(Seq_Data_Mem_dout), .out(C), .sel(src));

  // Other names for the same wires on the sheet: func_t[2:0] = func[2:0]
endmodule

module shifter_8bits (
  input  [7:0] A,
  input  [7:0] B,
  output [7:0] S
);

  wire or_1_out;
  wire [7:0] shifter_1_out;

  Shifter shifter_1 (.in(A), .\dist (B[2:0]), .out(shifter_1_out));
  Multiplexer #(.width(8)) multiplexer_1 (.in0(shifter_1_out), .in1({8{1'b0}}), .out(S), .sel(or_1_out));
  or or_1 (or_1_out, B[3], B[4], B[5], B[6], B[7]);
endmodule
