// Logisim project VLIW.circ as structural Verilog: 19 circuits, main circuit main
module main (
);

  wire BRZI, BRZR, CLK, H_OR_L, JR, MEM_TO_REG, MEM_W, or_1_out, REG_IMM_SRC, RESET, SAVEPC,
       soma_8bit_1_cout, W1, W2, W3, Z_FLAG;
  wire [1:0] multiplexer_3_out, multiplexer_4_out, RA1, RA2, RA3, RA4, RB1, RB2, RB3, RB4;
  wire [2:0] ALUOP1, ALUOP2;
  wire [3:0] OPCODE_ALU1, OPCODE_ALU2, OPCODE_CONTROL, OPCODE_DATA;
  wire [7:0] data_specialized_alu_1_out_4, ext_sig_4_8_1_out_2, multiplexer_1_out, multiplexer_2_out,
       multiplexer_5_out, multiplexer_6_out, PC_q, ram_1_dout, register_bank_1_control_a,
       register_bank_1_control_b, register_bank_1_data_a, register_bank_1_data_b, register_bank_1_ula1a,
       register_bank_1_ula1b, register_bank_1_ula2a, register_bank_1_ula2b, soma_8bit_1_sum, ula_8bit_1_c,
       ula_8bit_2_c;
  wire [31:0] rom_1_data;

  Multiplexer #(.width(8)) multiplexer_1 (
    .in0(soma_8bit_1_sum), .in1(register_bank_1_control_b), .out(multiplexer_1_out), .sel(or_1_out));
  or or_1 (or_1_out, JR, BRZR);
  Register PC (.D(multiplexer_1_out), .en(1'b1), .clk(CLK), .Q(PC_q), .clr(RESET));
  ROM #(.dataWidth(32)) rom_1 (.addr(PC_q), .data(rom_1_data));
  // Probe on PC_q
  SOMA_8BIT soma_8bit_1 (.a(PC_q), .b(multiplexer_2_out), .SUM(soma_8bit_1_sum), .Cout(soma_8bit_1_cout));
  // Probe on soma_8bit_1_cout
  // Probe on rom_1_data
  Multiplexer #(.width(8)) multiplexer_2 (.in0(8'h1), .in1(ext_sig_4_8_1_out_2), .out(multiplexer_2_out), .sel(BRZI));
  inst_handler inst_handler_1 (
    .INST_BIG(rom_1_data), .OPCODE1(OPCODE_DATA), .OPCODE2(OPCODE_CONTROL), .OPCODE3(OPCODE_ALU1),
    .OPCODE4(OPCODE_ALU2), .RA1(RA1), .RB1(RB1), .RA2(RA4), .RB2(RB4), .RA3(RA2), .RB3(RB2), .RA4(RA3),
    .RB4(RB3));
  Clock #(.highDuration(2), .lowDuration(2)) clock_1 (.out(CLK));
  Button button_1 (.out(RESET));
  Multiplexer #(.width(2)) multiplexer_3 (.in0(RA1), .in1(2'b00), .out(multiplexer_3_out), .sel(REG_IMM_SRC));
  Multiplexer #(.width(2)) multiplexer_4 (.in0(RA4), .in1(2'b00), .out(multiplexer_4_out), .sel(BRZI));
  REGISTER_BANK register_bank_1 (
    .D1(multiplexer_6_out), .D2(ula_8bit_1_c), .D3(ula_8bit_2_c), .RA1(multiplexer_3_out), .RB1(RB1),
    .RA2(RA2), .RB2(RB2), .RA3(RA3), .RB3(RB3), .RA4(multiplexer_4_out), .RB4(RB4), .w1(W1), .w2(W2),
    .w3(W3), .CLK(CLK), .RESET(RESET), .DATA_A(register_bank_1_data_a), .DATA_B(register_bank_1_data_b),
    .ULA1A(register_bank_1_ula1a), .ULA1B(register_bank_1_ula1b), .ULA2A(register_bank_1_ula2a),
    .ULA2B(register_bank_1_ula2b), .CONTROL_A(register_bank_1_control_a),
    .CONTROL_B(register_bank_1_control_b));
  EXT_SIG_4_8 ext_sig_4_8_1 (.in_1({RA1, RB1}), .out_2(ext_sig_4_8_1_out_2));
  CONT_MEM_UNIT cont_mem_unit_1 (
    .OPCODE_DATA(OPCODE_DATA), .OPCODE_CONTROL(OPCODE_CONTROL), .OPCODE_ALU1(OPCODE_ALU1),
    .OPCODE_ALU2(OPCODE_ALU2), .zero_flag(Z_FLAG), .SAVEPC(SAVEPC), .MEM_TO_REG(MEM_TO_REG), .MEM_W(MEM_W),
    .H_OR_L(H_OR_L), .REG_IMM_SRC(REG_IMM_SRC), .BRZR(BRZR), .JR(JR), .BRZI(BRZI), .ALUOP1(ALUOP1),
    .ALUOP2(ALUOP2), .REG_W1(W1), .REG_W2(W2), .REG_W3(W3));
  DATA_SPECIALIZED_ALU data_specialized_alu_1 (
    .a(register_bank_1_data_a), .b({RA1, RB1}), .HIGH_or_LOW(H_OR_L), .out_4(data_specialized_alu_1_out_4));
  ULA_8BIT ula_8bit_1 (.a(register_bank_1_ula1a), .b(register_bank_1_ula1b), .ALUOP(ALUOP1), .C(ula_8bit_1_c));
  ULA_8BIT ula_8bit_2 (.a(register_bank_1_ula2a), .b(register_bank_1_ula2b), .ALUOP(ALUOP2), .C(ula_8bit_2_c));
  CHECK_0 check_0_1 (.RA(register_bank_1_control_a), .ZERO_FLAG(Z_FLAG));
  RAM #(.trigger("falling")) ram_1 (
    .addr(register_bank_1_data_b), .we(MEM_W), .oe(1'b1), .clk(CLK), .din(register_bank_1_data_a),
    .dout(ram_1_dout));
  // Probe on ram_1_dout
  Multiplexer #(.width(8)) multiplexer_5 (
    .in0(data_specialized_alu_1_out_4), .in1(ram_1_dout), .out(multiplexer_5_out), .sel(MEM_TO_REG));
  Multiplexer #(.width(8)) multiplexer_6 (.in0(multiplexer_5_out), .in1(PC_q), .out(multiplexer_6_out), .sel(SAVEPC));

  // Notes on the sheet:
  //   contents of rom_1 (hex, n*v repeats v):
  //   7ff0f0f0 f0f088f0 f00bf0f0 71f0f0f0 f0f098f0 56f0f0f0 7cf0f0f0 f0f088f0 56f0f0f0 f0f088f0 56f0f0f0
  //   f0f098f0 f0f098f0 72f0f0f0 3ff0f0f0 f0f08cf0 f0f08cf0 f020f0f0 7cf0959f f0f088f0 60f0f0f0 72f0f0f0
  //   f0f08cf0 f00bf0f0 71f0f0f0 f0f098f0 5af0f0f0 7cf0f0f0 f0f086f0 f0f088f0 74f0f0f0 61f0f0f0 f0f084f0
  //   56f0f0f0 f0f095f0 60f0f0f0 7cf0f0f0 f0f098f0 74f0f0f0 61f0f0f0 3ff0f0f0 f020f0f0 70f0f0f0 7cf0959f
  //   f0f088f0 60f0f0f0 72f0f0f0 f0f08cf0 f00b9ff0 71f0f0f0 f0f098f0 4ef0f0f0 7cf0f0f0 f0f088f0 46f0f0f0
  //   f0f08788 56f09ff0 f0f09598 f0f098f0 7df0f0f0 62f0f0f0 3ff0f0f0 f020f0f0 72f09af0 3af0f0f0 f0f088f0
  //   f02af0f0
  //   DATA
  //   CONTROL
  //   ALU1
  //   ALU2
endmodule

module REGISTER_BANK (
  input  [7:0] D1,
  input  [7:0] D2,
  input  [7:0] D3,
  input  [1:0] RA1,
  input  [1:0] RB1,
  input  [1:0] RA2,
  input  [1:0] RB2,
  input  [1:0] RA3,
  input  [1:0] RB3,
  input  [1:0] RA4,
  input  [1:0] RB4,
  input  w1,
  input  w2,
  input  w3,
  input  CLK,
  input  RESET,
  output [7:0] DATA_A,
  output [7:0] DATA_B,
  output [7:0] ULA1A,
  output [7:0] ULA1B,
  output [7:0] ULA2A,
  output [7:0] ULA2B,
  output [7:0] CONTROL_A,
  output [7:0] CONTROL_B
);

  wire W0, W1_t, W2_t, W3_t;
  wire [7:0] D1_1, D1_2, D1_3, D1_4, D2_1, D2_2, D2_3, D2_4, D3_1, D3_2, D3_3, D3_4, or_1_out, or_2_out,
       or_3_out, or_4_out, OUT1, OUT2, OUT3, OUT4;

  Demultiplexer #(.select(2), .width(8)) demultiplexer_1 (
    .out0(D1_1), .out1(D1_2), .out2(D1_3), .out3(D1_4), .in(D1), .sel(RA1));
  Demultiplexer #(.select(2), .width(8)) demultiplexer_2 (
    .out0(D2_1), .out1(D2_2), .out2(D2_3), .out3(D2_4), .in(D2), .sel(RA2));
  Demultiplexer #(.select(2), .width(8)) demultiplexer_3 (
    .out0(D3_1), .out1(D3_2), .out2(D3_3), .out3(D3_4), .in(D3), .sel(RA3));
  write_control write_control_1 (
    .E1(RA1), .E2(RA2), .E3(RA3), .cont_mem_w1(w1), .cont_mem_w2(w2), .cont_mem_w3(w3), .W0(W0), .W1(W1_t),
    .W2(W2_t), .W3(W3_t));
  assign or_1_out = D1_1 | D2_1 | D3_1;  // OR_Gate or_1, 8 bits wide
  assign or_2_out = D1_2 | D2_2 | D3_2;  // OR_Gate or_2, 8 bits wide
  assign or_3_out = D1_3 | D2_3 | D3_3;  // OR_Gate or_3, 8 bits wide
  assign or_4_out = D1_4 | D2_4 | D3_4;  // OR_Gate or_4, 8 bits wide
  REGISTERS registers_1 (
    .IN1(or_1_out), .W1(W0), .IN2(or_2_out), .W2(W1_t), .IN3(or_3_out), .W3(W2_t), .IN4(or_4_out), .W4(W3_t),
    .CLK(CLK), .RESET(RESET), .OUT1(OUT1), .OUT2(OUT2), .OUT3(OUT3), .OUT4(OUT4));
  Multiplexer #(.select(2), .width(8)) multiplexer_1 (
    .in0(OUT1), .in1(OUT2), .in2(OUT3), .in3(OUT4), .out(DATA_A), .sel(RA1));
  Multiplexer #(.select(2), .width(8)) multiplexer_2 (
    .in0(OUT1), .in1(OUT2), .in2(OUT3), .in3(OUT4), .out(DATA_B), .sel(RB1));
  Multiplexer #(.select(2), .width(8)) multiplexer_3 (
    .in0(OUT1), .in1(OUT2), .in2(OUT3), .in3(OUT4), .out(ULA1A), .sel(RA2));
  Multiplexer #(.select(2), .width(8)) multiplexer_4 (
    .in0(OUT1), .in1(OUT2), .in2(OUT3), .in3(OUT4), .out(ULA1B), .sel(RB2));
  Multiplexer #(.select(2), .width(8)) multiplexer_5 (
    .in0(OUT1), .in1(OUT2), .in2(OUT3), .in3(OUT4), .out(ULA2A), .sel(RA3));
  Multiplexer #(.select(2), .width(8)) multiplexer_6 (
    .in0(OUT1), .in1(OUT2), .in2(OUT3), .in3(OUT4), .out(ULA2B), .sel(RB3));
  Multiplexer #(.select(2), .width(8)) multiplexer_7 (
    .in0(OUT1), .in1(OUT2), .in2(OUT3), .in3(OUT4), .out(CONTROL_A), .sel(RA4));
  Multiplexer #(.select(2), .width(8)) multiplexer_8 (
    .in0(OUT1), .in1(OUT2), .in2(OUT3), .in3(OUT4), .out(CONTROL_B), .sel(RB4));

  // Other names for the same wires on the sheet: R = RESET
endmodule

module SOMA_1BIT (
  input  a,
  input  b,
  input  Cin,
  output SUM,
  output Cout
);

  wire and_1_out, and_2_out, xor_1_out;

  xor xor_1 (xor_1_out, b, a);
  xor xor_2 (SUM, xor_1_out, Cin);
  and and_1 (and_1_out, xor_1_out, Cin);
  and and_2 (and_2_out, b, a);
  or or_1 (Cout, and_1_out, and_2_out);
endmodule

module SOMA_8BIT (
  input  [7:0] a,
  input  [7:0] b,
  output [7:0] SUM,
  output Cout
);

  wire soma_1bit_1_cout, soma_1bit_2_cout, soma_1bit_3_cout, soma_1bit_4_cout, soma_1bit_5_cout,
       soma_1bit_6_cout, soma_1bit_7_cout;

  SOMA_1BIT soma_1bit_1 (.a(a[0]), .b(b[0]), .Cin(1'b0), .SUM(SUM[0]), .Cout(soma_1bit_1_cout));
  SOMA_1BIT soma_1bit_2 (.a(a[1]), .b(b[1]), .Cin(soma_1bit_1_cout), .SUM(SUM[1]), .Cout(soma_1bit_2_cout));
  SOMA_1BIT soma_1bit_3 (.a(a[2]), .b(b[2]), .Cin(soma_1bit_2_cout), .SUM(SUM[2]), .Cout(soma_1bit_3_cout));
  SOMA_1BIT soma_1bit_4 (.a(a[3]), .b(b[3]), .Cin(soma_1bit_3_cout), .SUM(SUM[3]), .Cout(soma_1bit_4_cout));
  SOMA_1BIT soma_1bit_5 (.a(a[4]), .b(b[4]), .Cin(soma_1bit_4_cout), .SUM(SUM[4]), .Cout(soma_1bit_5_cout));
  SOMA_1BIT soma_1bit_6 (.a(a[5]), .b(b[5]), .Cin(soma_1bit_5_cout), .SUM(SUM[5]), .Cout(soma_1bit_6_cout));
  SOMA_1BIT soma_1bit_7 (.a(a[6]), .b(b[6]), .Cin(soma_1bit_6_cout), .SUM(SUM[6]), .Cout(soma_1bit_7_cout));
  SOMA_1BIT soma_1bit_8 (.a(a[7]), .b(b[7]), .Cin(soma_1bit_7_cout), .SUM(SUM[7]), .Cout(Cout));
endmodule

module ULA_8BIT (
  input  [7:0] a,
  input  [7:0] b,
  input  [2:0] ALUOP,
  output [7:0] C
);

  wire soma_8bit_1_cout, sub_8bit_1_cout;
  wire [7:0] and_1_out, not_1_out, or_1_out, shift_left_1_saida, shift_right_1_saida, soma_8bit_1_sum,
       sub_8bit_1_sum;

  assign not_1_out = ~b;  // NOT_Gate not_1, 8 bits wide
  assign and_1_out = a & b;  // AND_Gate and_1, 8 bits wide
  assign or_1_out = a | b;  // OR_Gate or_1, 8 bits wide
  SOMA_8BIT soma_8bit_1 (.a(a), .b(b), .SUM(soma_8bit_1_sum), .Cout(soma_8bit_1_cout));
  // Probe on soma_8bit_1_cout
  SUB_8BIT sub_8bit_1 (.a(a), .b(b), .SUM(sub_8bit_1_sum), .Cout(sub_8bit_1_cout));
  // Probe on sub_8bit_1_cout
  SHIFT_LEFT shift_left_1 (.a(a), .b(b), .saida(shift_left_1_saida));
  SHIFT_RIGHT shift_right_1 (.a(a), .b(b), .saida(shift_right_1_saida));
  Multiplexer #(.select(3), .width(8)) multiplexer_1 (
    .in0({8{1'b0}}), .in1(soma_8bit_1_sum), .in2(sub_8bit_1_sum), .in3(not_1_out), .in4(or_1_out),
    .in5(shift_left_1_saida), .in6(shift_right_1_saida), .in7(and_1_out), .out(C), .sel(ALUOP));
endmodule

module SHIFT_LEFT (
  input  [7:0] a,
  input  [7:0] b,
  output [7:0] saida
);

  wire multiplexer_1_out, multiplexer_2_out, multiplexer_3_out, multiplexer_4_out, multiplexer_5_out,
       multiplexer_6_out, multiplexer_7_out, multiplexer_8_out, multiplexer_9_out, multiplexer_10_out,
       multiplexer_11_out, multiplexer_12_out, multiplexer_13_out, multiplexer_14_out, multiplexer_15_out,
       multiplexer_16_out, S3;
  wire [7:0] multiplexer_17_out;

  or or_1 (S3, b[3], b[4], b[5], b[6], b[7]);
  Multiplexer multiplexer_1 (.in0(a[0]), .in1(1'b0), .out(multiplexer_1_out), .sel(b[0]));
  Multiplexer multiplexer_2 (.in0(a[1]), .in1(a[0]), .out(multiplexer_2_out), .sel(b[0]));
  Multiplexer multiplexer_3 (.in0(a[2]), .in1(a[1]), .out(multiplexer_3_out), .sel(b[0]));
  Multiplexer multiplexer_4 (.in0(a[3]), .in1(a[2]), .out(multiplexer_4_out), .sel(b[0]));
  Multiplexer multiplexer_5 (.in0(a[4]), .in1(a[3]), .out(multiplexer_5_out), .sel(b[0]));
  Multiplexer multiplexer_6 (.in0(a[5]), .in1(a[4]), .out(multiplexer_6_out), .sel(b[0]));
  Multiplexer multiplexer_7 (.in0(a[6]), .in1(a[5]), .out(multiplexer_7_out), .sel(b[0]));
  Multiplexer multiplexer_8 (.in0(a[7]), .in1(a[6]), .out(multiplexer_8_out), .sel(b[0]));
  Multiplexer multiplexer_9 (.in0(multiplexer_1_out), .in1(1'b0), .out(multiplexer_9_out), .sel(b[1]));
  Multiplexer multiplexer_10 (.in0(multiplexer_2_out), .in1(1'b0), .out(multiplexer_10_out), .sel(b[1]));
  Multiplexer multiplexer_11 (.in0(multiplexer_3_out), .in1(multiplexer_1_out), .out(multiplexer_11_out), .sel(b[1]));
  Multiplexer multiplexer_12 (.in0(multiplexer_4_out), .in1(multiplexer_2_out), .out(multiplexer_12_out), .sel(b[1]));
  Multiplexer multiplexer_13 (.in0(multiplexer_5_out), .in1(multiplexer_3_out), .out(multiplexer_13_out), .sel(b[1]));
  Multiplexer multiplexer_14 (.in0(multiplexer_6_out), .in1(multiplexer_4_out), .out(multiplexer_14_out), .sel(b[1]));
  Multiplexer multiplexer_15 (.in0(multiplexer_7_out), .in1(multiplexer_5_out), .out(multiplexer_15_out), .sel(b[1]));
  Multiplexer multiplexer_16 (.in0(multiplexer_8_out), .in1(multiplexer_6_out), .out(multiplexer_16_out), .sel(b[1]));
  Multiplexer multiplexer_17 (.in0(multiplexer_9_out), .in1(1'b0), .out(multiplexer_17_out[0]), .sel(b[2]));
  Multiplexer multiplexer_18 (.in0(multiplexer_10_out), .in1(1'b0), .out(multiplexer_17_out[1]), .sel(b[2]));
  Multiplexer multiplexer_19 (.in0(multiplexer_11_out), .in1(1'b0), .out(multiplexer_17_out[2]), .sel(b[2]));
  Multiplexer multiplexer_20 (.in0(multiplexer_12_out), .in1(1'b0), .out(multiplexer_17_out[3]), .sel(b[2]));
  Multiplexer multiplexer_21 (
    .in0(multiplexer_13_out), .in1(multiplexer_9_out), .out(multiplexer_17_out[4]), .sel(b[2]));
  Multiplexer multiplexer_22 (
    .in0(multiplexer_14_out), .in1(multiplexer_10_out), .out(multiplexer_17_out[5]), .sel(b[2]));
  Multiplexer multiplexer_23 (
    .in0(multiplexer_15_out), .in1(multiplexer_11_out), .out(multiplexer_17_out[6]), .sel(b[2]));
  Multiplexer multiplexer_24 (
    .in0(multiplexer_16_out), .in1(multiplexer_12_out), .out(multiplexer_17_out[7]), .sel(b[2]));
  Multiplexer #(.width(8)) multiplexer_25 (.in0(multiplexer_17_out), .in1({8{1'b0}}), .out(saida), .sel(S3));

  // Other names for the same wires on the sheet: S = b[0]; S1 = b[1]; S2 = b[2]
endmodule

module SHIFT_RIGHT (
  input  [7:0] a,
  input  [7:0] b,
  output [7:0] saida
);

  wire multiplexer_1_out, multiplexer_2_out, multiplexer_3_out, multiplexer_4_out, multiplexer_5_out,
       multiplexer_6_out, multiplexer_7_out, multiplexer_8_out, multiplexer_9_out, multiplexer_10_out,
       multiplexer_11_out, multiplexer_12_out, multiplexer_13_out, multiplexer_14_out, multiplexer_15_out,
       multiplexer_16_out, S3;
  wire [7:0] multiplexer_17_out;

  or or_1 (S3, b[3], b[4], b[5], b[6], b[7]);
  Multiplexer multiplexer_1 (.in0(a[0]), .in1(a[1]), .out(multiplexer_1_out), .sel(b[0]));
  Multiplexer multiplexer_2 (.in0(a[1]), .in1(a[2]), .out(multiplexer_2_out), .sel(b[0]));
  Multiplexer multiplexer_3 (.in0(a[2]), .in1(a[3]), .out(multiplexer_3_out), .sel(b[0]));
  Multiplexer multiplexer_4 (.in0(a[3]), .in1(a[4]), .out(multiplexer_4_out), .sel(b[0]));
  Multiplexer multiplexer_5 (.in0(a[4]), .in1(a[5]), .out(multiplexer_5_out), .sel(b[0]));
  Multiplexer multiplexer_6 (.in0(a[5]), .in1(a[6]), .out(multiplexer_6_out), .sel(b[0]));
  Multiplexer multiplexer_7 (.in0(a[6]), .in1(a[7]), .out(multiplexer_7_out), .sel(b[0]));
  Multiplexer multiplexer_8 (.in0(a[7]), .in1(1'b0), .out(multiplexer_8_out), .sel(b[0]));
  Multiplexer multiplexer_9 (.in0(multiplexer_1_out), .in1(multiplexer_3_out), .out(multiplexer_9_out), .sel(b[1]));
  Multiplexer multiplexer_10 (.in0(multiplexer_2_out), .in1(multiplexer_4_out), .out(multiplexer_10_out), .sel(b[1]));
  Multiplexer multiplexer_11 (.in0(multiplexer_3_out), .in1(multiplexer_5_out), .out(multiplexer_11_out), .sel(b[1]));
  Multiplexer multiplexer_12 (.in0(multiplexer_4_out), .in1(multiplexer_6_out), .out(multiplexer_12_out), .sel(b[1]));
  Multiplexer multiplexer_13 (.in0(multiplexer_5_out), .in1(multiplexer_7_out), .out(multiplexer_13_out), .sel(b[1]));
  Multiplexer multiplexer_14 (.in0(multiplexer_6_out), .in1(multiplexer_8_out), .out(multiplexer_14_out), .sel(b[1]));
  Multiplexer multiplexer_15 (.in0(multiplexer_7_out), .in1(1'b0), .out(multiplexer_15_out), .sel(b[1]));
  Multiplexer multiplexer_16 (.in0(multiplexer_8_out), .in1(1'b0), .out(multiplexer_16_out), .sel(b[1]));
  Multiplexer multiplexer_17 (
    .in0(multiplexer_9_out), .in1(multiplexer_13_out), .out(multiplexer_17_out[0]), .sel(b[2]));
  Multiplexer multiplexer_18 (
    .in0(multiplexer_10_out), .in1(multiplexer_14_out), .out(multiplexer_17_out[1]), .sel(b[2]));
  Multiplexer multiplexer_19 (
    .in0(multiplexer_11_out), .in1(multiplexer_15_out), .out(multiplexer_17_out[2]), .sel(b[2]));
  Multiplexer multiplexer_20 (
    .in0(multiplexer_12_out), .in1(multiplexer_16_out), .out(multiplexer_17_out[3]), .sel(b[2]));
  Multiplexer multiplexer_21 (.in0(multiplexer_13_out), .in1(1'b0), .out(multiplexer_17_out[4]), .sel(b[2]));
  Multiplexer multiplexer_22 (.in0(multiplexer_14_out), .in1(1'b0), .out(multiplexer_17_out[5]), .sel(b[2]));
  Multiplexer multiplexer_23 (.in0(multiplexer_15_out), .in1(1'b0), .out(multiplexer_17_out[6]), .sel(b[2]));
  Multiplexer multiplexer_24 (.in0(multiplexer_16_out), .in1(1'b0), .out(multiplexer_17_out[7]), .sel(b[2]));
  Multiplexer #(.width(8)) multiplexer_25 (.in0(multiplexer_17_out), .in1({8{1'b0}}), .out(saida), .sel(S3));

  // Other names for the same wires on the sheet: S = b[0]; S1 = b[1]; S2 = b[2]
endmodule

module SUB_8BIT (
  input  [7:0] a,
  input  [7:0] b,
  output [7:0] SUM,
  output Cout
);

  wire soma_1bit_1_cout, soma_1bit_2_cout, soma_1bit_3_cout, soma_1bit_4_cout, soma_1bit_5_cout,
       soma_1bit_6_cout, soma_1bit_7_cout;
  wire [7:0] not_1_out;

  assign not_1_out = ~b;  // NOT_Gate not_1, 8 bits wide
  SOMA_1BIT soma_1bit_1 (.a(a[0]), .b(not_1_out[0]), .Cin(1'b1), .SUM(SUM[0]), .Cout(soma_1bit_1_cout));
  SOMA_1BIT soma_1bit_2 (.a(a[1]), .b(not_1_out[1]), .Cin(soma_1bit_1_cout), .SUM(SUM[1]), .Cout(soma_1bit_2_cout));
  SOMA_1BIT soma_1bit_3 (.a(a[2]), .b(not_1_out[2]), .Cin(soma_1bit_2_cout), .SUM(SUM[2]), .Cout(soma_1bit_3_cout));
  SOMA_1BIT soma_1bit_4 (.a(a[3]), .b(not_1_out[3]), .Cin(soma_1bit_3_cout), .SUM(SUM[3]), .Cout(soma_1bit_4_cout));
  SOMA_1BIT soma_1bit_5 (.a(a[4]), .b(not_1_out[4]), .Cin(soma_1bit_4_cout), .SUM(SUM[4]), .Cout(soma_1bit_5_cout));
  SOMA_1BIT soma_1bit_6 (.a(a[5]), .b(not_1_out[5]), .Cin(soma_1bit_5_cout), .SUM(SUM[5]), .Cout(soma_1bit_6_cout));
  SOMA_1BIT soma_1bit_7 (.a(a[6]), .b(not_1_out[6]), .Cin(soma_1bit_6_cout), .SUM(SUM[6]), .Cout(soma_1bit_7_cout));
  SOMA_1BIT soma_1bit_8 (.a(a[7]), .b(not_1_out[7]), .Cin(soma_1bit_7_cout), .SUM(SUM[7]), .Cout(Cout));
endmodule

module EXT_SIG_4_8 (
  input  [3:0] in_1,
  output [7:0] out_2
);


  assign out_2 = {{5{in_1[3]}}, in_1[2:0]};
endmodule

module inst_handler (
  input  [31:0] INST_BIG,
  output [3:0] OPCODE1,
  output [1:0] RA1,
  output [1:0] RB1,
  output [3:0] OPCODE2,
  output [1:0] RA2,
  output [1:0] RB2,
  output [3:0] OPCODE3,
  output [1:0] RA3,
  output [1:0] RB3,
  output [3:0] OPCODE4,
  output [1:0] RA4,
  output [1:0] RB4
);

  // Probe on INST_BIG[31:24]
  // Probe on INST_BIG[23:16]
  // Probe on INST_BIG[15:8]
  // Probe on INST_BIG[7:0]

  assign OPCODE1 = INST_BIG[31:28];
  assign OPCODE2 = INST_BIG[23:20];
  assign OPCODE3 = INST_BIG[15:12];
  assign OPCODE4 = INST_BIG[7:4];
  assign RA1 = INST_BIG[27:26];
  assign RA2 = INST_BIG[19:18];
  assign RA3 = INST_BIG[11:10];
  assign RA4 = INST_BIG[3:2];
  assign RB1 = INST_BIG[25:24];
  assign RB2 = INST_BIG[17:16];
  assign RB3 = INST_BIG[9:8];
  assign RB4 = INST_BIG[1:0];
endmodule

module REGISTERS (
  input  [7:0] IN1,
  input  W1,
  input  [7:0] IN2,
  input  W2,
  input  [7:0] IN3,
  input  W3,
  input  [7:0] IN4,
  input  W4,
  input  CLK,
  input  RESET,
  output [7:0] OUT1,
  output [7:0] OUT2,
  output [7:0] OUT3,
  output [7:0] OUT4
);

  Register register_1 (.D(IN1), .en(W1), .clk(CLK), .Q(OUT1), .clr(RESET));
  Register register_2 (.D(IN2), .en(W2), .clk(CLK), .Q(OUT2), .clr(RESET));
  Register register_3 (.D(IN3), .en(W3), .clk(CLK), .Q(OUT3), .clr(RESET));
  Register register_4 (.D(IN4), .en(W4), .clk(CLK), .Q(OUT4), .clr(RESET));

  // Other names for the same wires on the sheet: R = RESET
endmodule

module DATA_SPECIALIZED_ALU (
  input  [7:0] a,
  input  [3:0] b,
  input  HIGH_or_LOW,
  output [7:0] out_4
);

  Multiplexer #(.width(8)) multiplexer_1 (.in0({b, a[3:0]}), .in1({a[7:4], b}), .out(out_4), .sel(HIGH_or_LOW));

  // Notes on the sheet:
  //   MOVE_HIGH
  //   MOVE_LOW
endmodule

module CHECK_0 (
  input  [7:0] RA,
  output ZERO_FLAG
);

  wire not_1_out, not_2_out, not_3_out, not_4_out, not_5_out, not_6_out, not_7_out, not_8_out;

  not not_1 (not_1_out, RA[0]);
  not not_2 (not_2_out, RA[1]);
  not not_3 (not_3_out, RA[2]);
  not not_4 (not_4_out, RA[3]);
  not not_5 (not_5_out, RA[4]);
  not not_6 (not_6_out, RA[5]);
  not not_7 (not_7_out, RA[6]);
  not not_8 (not_8_out, RA[7]);
  and and_1 (ZERO_FLAG, not_1_out, not_2_out, not_3_out, not_4_out, not_5_out, not_6_out, not_7_out, not_8_out);
endmodule

module write_control (
  input  [1:0] E1,
  input  [1:0] E2,
  input  [1:0] E3,
  input  cont_mem_w1,
  input  cont_mem_w2,
  input  cont_mem_w3,
  output W0,
  output W1,
  output W2,
  output W3
);

  wire demultiplexer_1_out0, demultiplexer_1_out1, demultiplexer_1_out2, demultiplexer_1_out3,
       demultiplexer_2_out0, demultiplexer_2_out1, demultiplexer_2_out2, demultiplexer_2_out3,
       demultiplexer_3_out0, demultiplexer_3_out1, demultiplexer_3_out2, demultiplexer_3_out3;

  Demultiplexer #(.select(2)) demultiplexer_1 (
    .out0(demultiplexer_1_out0), .out1(demultiplexer_1_out1), .out2(demultiplexer_1_out2),
    .out3(demultiplexer_1_out3), .in(cont_mem_w1), .sel(E1));
  Demultiplexer #(.select(2)) demultiplexer_2 (
    .out0(demultiplexer_2_out0), .out1(demultiplexer_2_out1), .out2(demultiplexer_2_out2),
    .out3(demultiplexer_2_out3), .in(cont_mem_w2), .sel(E2));
  Demultiplexer #(.select(2)) demultiplexer_3 (
    .out0(demultiplexer_3_out0), .out1(demultiplexer_3_out1), .out2(demultiplexer_3_out2),
    .out3(demultiplexer_3_out3), .in(cont_mem_w3), .sel(E3));
  or or_1 (W0, demultiplexer_1_out0, demultiplexer_2_out0, demultiplexer_3_out0);
  or or_2 (W1, demultiplexer_1_out1, demultiplexer_2_out1, demultiplexer_3_out1);
  or or_3 (W2, demultiplexer_1_out2, demultiplexer_2_out2, demultiplexer_3_out2);
  or or_4 (W3, demultiplexer_1_out3, demultiplexer_2_out3, demultiplexer_3_out3);

  // Other names for the same wires on the sheet: W1_t = cont_mem_w1; W2_t = cont_mem_w2; W3_t = cont_mem_w3
endmodule

module ALU_CONT_MEM (
  input  [3:0] OPCODE_ALU,
  output [2:0] ALUOP,
  output REG_W
);

  ROM #(.addrWidth(4), .dataWidth(4)) rom_1 (.addr(OPCODE_ALU), .data({ALUOP, REG_W}));
  // Probe on {ALUOP, REG_W}

  // Notes on the sheet:
  //   contents of rom_1 (hex, n*v repeats v):
  //   8*0 3 5 f 9 7 b d
endmodule

module DATA_CONT_MEM (
  input  [3:0] in_1,
  output SAVEPC,
  output MEM_to_REG,
  output MEM_W,
  output HorL,
  output REG_IMM_SRC,
  output REG_W
);

  ROM #(.addrWidth(4), .dataWidth(6)) rom_1 (.addr(in_1), .data({SAVEPC, MEM_to_REG, MEM_W, HorL, REG_IMM_SRC, REG_W}));

  // Notes on the sheet:
  //   contents of rom_1 (hex, n*v repeats v):
  //   0 0 0 21 11 8 3 7
endmodule

module CONTROL_CONT_MEM (
  input  [3:0] in_1,
  output BRZR,
  output JR,
  output BRZI
);

  ROM #(.addrWidth(4), .dataWidth(3)) rom_1 (.addr(in_1), .data({BRZR, JR, BRZI}));

  // Notes on the sheet:
  //   contents of rom_1 (hex, n*v repeats v):
  //   4 1 2
endmodule

module CONT_MEM_UNIT (
  input  [3:0] OPCODE_DATA,
  input  [3:0] OPCODE_CONTROL,
  input  [3:0] OPCODE_ALU1,
  input  [3:0] OPCODE_ALU2,
  input  zero_flag,
  output SAVEPC,
  output MEM_TO_REG,
  output MEM_W,
  output H_OR_L,
  output REG_IMM_SRC,
  output BRZR,
  output JR,
  output BRZI,
  output [2:0] ALUOP1,
  output [2:0] ALUOP2,
  output REG_W1,
  output REG_W2,
  output REG_W3
);

  wire control_cont_mem_1_brzi, control_cont_mem_1_brzr;

  DATA_CONT_MEM data_cont_mem_1 (
    .in_1(OPCODE_DATA), .SAVEPC(SAVEPC), .MEM_to_REG(MEM_TO_REG), .MEM_W(MEM_W), .HorL(H_OR_L),
    .REG_IMM_SRC(REG_IMM_SRC), .REG_W(REG_W1));
  CONTROL_CONT_MEM control_cont_mem_1 (
    .in_1(OPCODE_CONTROL), .BRZR(control_cont_mem_1_brzr), .JR(JR), .BRZI(control_cont_mem_1_brzi));
  ALU_CONT_MEM alu_cont_mem_1 (.OPCODE_ALU(OPCODE_ALU1), .ALUOP(ALUOP1), .REG_W(REG_W2));
  ALU_CONT_MEM alu_cont_mem_2 (.OPCODE_ALU(OPCODE_ALU2), .ALUOP(ALUOP2), .REG_W(REG_W3));
  and and_1 (BRZR, control_cont_mem_1_brzr, zero_flag);
  and and_2 (BRZI, control_cont_mem_1_brzi, zero_flag);

  // Other names for the same wires on the sheet: W1 = REG_W1; W2 = REG_W2; W3 = REG_W3; Z_FLAG = zero_flag
endmodule

module test (
  input  [7:0] in_1,
  input  [7:0] in_2,
  input  [7:0] in_3
);

  wire undriven;

  RAM ram_1 (.addr(in_1), .we(undriven), .din(in_2), .dout(in_3));  // open: oe, clk
endmodule
